// Logisim project CPU design .circ as structural Verilog: 4 circuits, main circuit main
module main (
  input  [1:0] in_1,
  input  [7:0] in_2,
  input  [1:0] in_3,
  input  in_4,
  input  [7:0] in_5,
  input  [1:0] in_6,
  input  in_7,
  input  in_8,
  input  [3:0] in_9,
  input  in_10,
  input  in_11,
  output [3:0] out_12,
  output [7:0] out_13,
  output [3:0] out_14,
  output out_15
);

  wire clk_1_clock_out, clock_1_out, clock_2_out;

  Clock clock_1 (.out(clock_1_out));
  LED led_1 (.in(clk_1_clock_out));
  CLK clk_1 (.CLK_IN(clock_1_out), .CLK_ENB(in_4), .Manual_clock(in_7), .HALT(in_11), .Clock_Out(clk_1_clock_out));
  _4bit_register u_4bit_register_1 (
    .regWrite(in_10), .Read_Register_1(in_1), .Read_Register_2(in_3), .write_data(in_9),
    .read_data_1(out_12), .read_data_2(out_14), .write_Register(in_6), .Clk(in_10));
  Clock clock_2 (.out(clock_2_out));
  Memory memory_1 (
    .Address_Input(in_2), .Data_Input(in_5), .Write_Enable__Store(in_8), .Data_Out(out_13),
    .Load_Status__Read_Mode(out_15));
endmodule

module CLK (
  input  CLK_IN,
  input  CLK_ENB,
  input  Manual_clock,
  input  HALT,
  output Clock_Out
);

  wire and_1_out, and_2_out, not_1_out, not_2_out, or_1_out;

  not not_1 (not_1_out, CLK_ENB);
  not not_2 (not_2_out, HALT);
  and and_1 (and_1_out, CLK_IN, CLK_ENB);
  and and_2 (and_2_out, not_1_out, Manual_clock);
  or or_1 (or_1_out, and_1_out, and_2_out);
  and and_3 (Clock_Out, or_1_out, not_2_out);

  // Notes on the sheet:
  //   CLOCK
endmodule

module _4bit_register (
  input  [1:0] write_Register,
  input  regWrite,
  input  Clk,
  input  [1:0] Read_Register_1,
  input  [1:0] Read_Register_2,
  input  [3:0] write_data,
  output [3:0] read_data_1,
  output [3:0] read_data_2
);

  wire and_1_out, and_2_out, and_3_out, and_4_out, decoder_1_out0, decoder_1_out1, decoder_1_out2,
       decoder_1_out3;
  wire [3:0] register_1_q, register_2_q, register_3_q, register_4_q;

  Decoder #(.select(2)) decoder_1 (
    .out0(decoder_1_out0), .out1(decoder_1_out1), .out2(decoder_1_out2), .out3(decoder_1_out3),
    .sel(write_Register));  // open: en
  and and_1 (and_1_out, decoder_1_out0, regWrite);
  and and_2 (and_2_out, decoder_1_out1, regWrite);
  and and_3 (and_3_out, decoder_1_out2, regWrite);
  and and_4 (and_4_out, decoder_1_out3, regWrite);
  Register #(.width(4)) register_1 (.D(write_data), .en(and_1_out), .Q(register_1_q), .clk(Clk));  // open: clr
  Register #(.width(4)) register_2 (.D(write_data), .en(and_2_out), .Q(register_2_q), .clk(Clk));  // open: clr
  Register #(.width(4)) register_3 (.D(write_data), .en(and_3_out), .Q(register_3_q), .clk(Clk));  // open: clr
  Register #(.width(4)) register_4 (.D(write_data), .en(and_4_out), .Q(register_4_q), .clk(Clk));  // open: clr
  Multiplexer #(.select(2), .width(4)) multiplexer_1 (
    .in0(register_1_q), .in1(register_2_q), .in2(register_3_q), .in3(register_4_q), .out(read_data_1),
    .sel(Read_Register_1));  // open: en
  Multiplexer #(.select(2), .width(4)) multiplexer_2 (
    .in0(register_1_q), .in1(register_2_q), .in2(register_3_q), .in3(register_4_q), .out(read_data_2),
    .sel(Read_Register_2));  // open: en

  // Notes on the sheet:
  //   4bit Register
endmodule

module Memory (
  input  [7:0] Address_Input,
  input  [7:0] Data_Input,
  input  Write_Enable__Store,
  output [7:0] Data_Out,
  output Load_Status__Read_Mode
);

  wire clock_1_out;

  Clock clock_1 (.out(clock_1_out));
  RAM #(.bus("separate")) ram_1 (
    .addr(Address_Input), .din(Data_Input), .data(Data_Out), .str(Write_Enable__Store), .sel(1'b1),
    .clk(clock_1_out), .ld(1'b1), .clr(1'b0));
  not not_1 (Load_Status__Read_Mode, Write_Enable__Store);

  // Notes on the sheet:
  //   Memory (RAM)
endmodule
